// Logisim project Clock_Logiscm.circ as structural Verilog: 14 circuits, main circuit main
module L_3_bit_adder_2dd98d25 (
  input  in_1,
  input  in_2,
  input  in_3,
  output out_4,
  output out_5,
  output out_6
);

  wire and_1_out, j_k_ff_1_qn, j_k_ff_2_qn, not_1_out, or_1_out;

  J_K_Flip_Flop j_k_ff_1 (
    .J(in_1), .K(in_1), .clk(in_3), .Q(out_4), .Qn(j_k_ff_1_qn), .reset(or_1_out));  // open: preset
  J_K_Flip_Flop j_k_ff_2 (
    .J(in_1), .K(in_1), .clk(j_k_ff_1_qn), .Q(out_5), .Qn(j_k_ff_2_qn), .reset(or_1_out));  // open: preset
  not not_1 (not_1_out, out_4);
  J_K_Flip_Flop j_k_ff_3 (.J(in_1), .K(in_1), .clk(j_k_ff_2_qn), .Q(out_6), .reset(or_1_out));  // open: Qn, preset
  and and_1 (and_1_out, out_6, out_5, not_1_out);
  or or_1 (or_1_out, and_1_out, in_2);
endmodule

module main (
  input  in_1
);

  wire and_1_out, and_2_out, and_3_out, and_4_out, and_5_out, and_6_out, and_7_out, and_8_out, and_9_out,
       and_10_out, and_11_out, clock_1_out, l_3_bit_adder_2dd98d25_1_out_4, l_3_bit_adder_2dd98d25_1_out_5,
       l_3_bit_adder_2dd98d25_1_out_6, l_3_bit_adder_2dd98d25_2_out_4, l_3_bit_adder_2dd98d25_2_out_5,
       l_3_bit_adder_2dd98d25_2_out_6, l_4bitreset_c5035a69_1_b0, l_4bitreset_c5035a69_1_b1,
       l_4bitreset_c5035a69_1_b2, l_4bitreset_c5035a69_1_b3, l_4bitreset_c5035a69_2_b0,
       l_4bitreset_c5035a69_2_b1, l_4bitreset_c5035a69_2_b2, l_4bitreset_c5035a69_2_b3,
       l_4bitreset_c5035a69_3_b0, l_4bitreset_c5035a69_3_b1, l_4bitreset_c5035a69_3_b2,
       l_4bitreset_c5035a69_3_b3, not_1_out, not_2_out, not_3_out, not_4_out, not_5_out, not_6_out,
       not_7_out, not_8_out, sevenseg_1_a, sevenseg_1_b, sevenseg_1_c, sevenseg_1_d, sevenseg_1_e,
       sevenseg_1_f, sevenseg_1_g, sevenseg_2_a, sevenseg_2_b, sevenseg_2_c, sevenseg_2_d, sevenseg_2_e,
       sevenseg_2_f, sevenseg_2_g, sevenseg_3_a, sevenseg_3_b, sevenseg_3_c, sevenseg_3_d, sevenseg_3_e,
       sevenseg_3_f, sevenseg_3_g, sevenseg_4_a, sevenseg_4_b, sevenseg_4_c, sevenseg_4_d, sevenseg_4_e,
       sevenseg_4_f, sevenseg_4_g, sevenseg_5_a, sevenseg_5_b, sevenseg_5_c, sevenseg_5_d, sevenseg_5_e,
       sevenseg_5_f, sevenseg_5_g, sevenseg_6_a, sevenseg_6_b, sevenseg_6_c, sevenseg_6_d, sevenseg_6_e,
       sevenseg_6_f, sevenseg_6_g, twobitmodthree_1_out_4, twobitmodthree_1_out_5;

  and and_1 (and_1_out, and_2_out, and_3_out);
  twobitmodthree twobitmodthree_1 (
    .in_1(and_8_out), .in_3(clock_1_out), .in_2(and_1_out), .out_4(twobitmodthree_1_out_4),
    .out_5(twobitmodthree_1_out_5));
  and and_2 (and_2_out, and_9_out, and_5_out);
  and and_3 (and_3_out, l_4bitreset_c5035a69_1_b0, l_4bitreset_c5035a69_1_b3);
  sevenseg sevenseg_1 (
    .B0(twobitmodthree_1_out_4), .B1(twobitmodthree_1_out_5), .B2(1'b0), .B3(1'b0), .a(sevenseg_1_a),
    .b(sevenseg_1_b), .c(sevenseg_1_c), .d(sevenseg_1_d), .e(sevenseg_1_e), .f(sevenseg_1_f), .g(sevenseg_1_g));
  L_4bitreset_c5035a69 l_4bitreset_c5035a69_1 (
    .Enable(and_2_out), .Clk(clock_1_out), .in_3(and_8_out), .B2(l_4bitreset_c5035a69_1_b2),
    .b1(l_4bitreset_c5035a69_1_b1), .B3(l_4bitreset_c5035a69_1_b3), .B0(l_4bitreset_c5035a69_1_b0));  // open: Co
  sevenseg sevenseg_2 (
    .B0(l_4bitreset_c5035a69_1_b0), .B1(l_4bitreset_c5035a69_1_b1), .B2(l_4bitreset_c5035a69_1_b2),
    .B3(l_4bitreset_c5035a69_1_b3), .a(sevenseg_2_a), .b(sevenseg_2_b), .c(sevenseg_2_c), .d(sevenseg_2_d),
    .e(sevenseg_2_e), .f(sevenseg_2_f), .g(sevenseg_2_g));
  _7_Segment_Display u_7_segment_display_1 (
    .g(sevenseg_1_g), .f(sevenseg_1_f), .a(sevenseg_1_a), .b(sevenseg_1_b), .e(sevenseg_1_e),
    .d(sevenseg_1_d), .c(sevenseg_1_c));  // open: dp
  and and_4 (and_4_out, l_3_bit_adder_2dd98d25_1_out_4, l_3_bit_adder_2dd98d25_1_out_6);
  and and_5 (and_5_out, and_4_out, and_7_out);
  _7_Segment_Display u_7_segment_display_2 (
    .g(sevenseg_2_g), .f(sevenseg_2_f), .a(sevenseg_2_a), .b(sevenseg_2_b), .e(sevenseg_2_e),
    .d(sevenseg_2_d), .c(sevenseg_2_c));  // open: dp
  L_3_bit_adder_2dd98d25 l_3_bit_adder_2dd98d25_1 (
    .in_2(and_8_out), .in_3(and_6_out), .in_1(clock_1_out), .out_6(l_3_bit_adder_2dd98d25_1_out_6),
    .out_4(l_3_bit_adder_2dd98d25_1_out_4), .out_5(l_3_bit_adder_2dd98d25_1_out_5));
  and and_6 (and_6_out, not_1_out, not_2_out, not_3_out, not_4_out);
  sevenseg sevenseg_3 (
    .B0(l_3_bit_adder_2dd98d25_1_out_4), .B1(l_3_bit_adder_2dd98d25_1_out_5),
    .B2(l_3_bit_adder_2dd98d25_1_out_6), .B3(1'b0), .a(sevenseg_3_a), .b(sevenseg_3_b), .c(sevenseg_3_c),
    .d(sevenseg_3_d), .e(sevenseg_3_e), .f(sevenseg_3_f), .g(sevenseg_3_g));
  and and_7 (and_7_out, l_4bitreset_c5035a69_2_b3, l_4bitreset_c5035a69_2_b0);
  and and_8 (and_8_out, l_4bitreset_c5035a69_1_b2, twobitmodthree_1_out_5);
  _7_Segment_Display u_7_segment_display_3 (
    .g(sevenseg_3_g), .f(sevenseg_3_f), .a(sevenseg_3_a), .b(sevenseg_3_b), .e(sevenseg_3_e),
    .d(sevenseg_3_d), .c(sevenseg_3_c));  // open: dp
  L_4bitreset_c5035a69 l_4bitreset_c5035a69_2 (
    .Enable(and_9_out), .Clk(clock_1_out), .in_3(and_8_out), .B2(l_4bitreset_c5035a69_2_b2),
    .b1(l_4bitreset_c5035a69_2_b1), .B3(l_4bitreset_c5035a69_2_b3), .B0(l_4bitreset_c5035a69_2_b0));  // open: Co
  not not_1 (not_1_out, l_4bitreset_c5035a69_2_b3);
  not not_2 (not_2_out, l_4bitreset_c5035a69_2_b2);
  not not_3 (not_3_out, l_4bitreset_c5035a69_2_b1);
  not not_4 (not_4_out, l_4bitreset_c5035a69_2_b0);
  and and_9 (and_9_out, l_3_bit_adder_2dd98d25_2_out_6, l_3_bit_adder_2dd98d25_2_out_4, and_11_out);
  L_3_bit_adder_2dd98d25 l_3_bit_adder_2dd98d25_2 (
    .in_2(and_8_out), .in_3(and_10_out), .in_1(clock_1_out), .out_6(l_3_bit_adder_2dd98d25_2_out_6),
    .out_4(l_3_bit_adder_2dd98d25_2_out_4), .out_5(l_3_bit_adder_2dd98d25_2_out_5));
  sevenseg sevenseg_4 (
    .B0(l_4bitreset_c5035a69_2_b0), .B1(l_4bitreset_c5035a69_2_b1), .B2(l_4bitreset_c5035a69_2_b2),
    .B3(l_4bitreset_c5035a69_2_b3), .a(sevenseg_4_a), .b(sevenseg_4_b), .c(sevenseg_4_c), .d(sevenseg_4_d),
    .e(sevenseg_4_e), .f(sevenseg_4_f), .g(sevenseg_4_g));
  _7_Segment_Display u_7_segment_display_4 (
    .g(sevenseg_4_g), .f(sevenseg_4_f), .a(sevenseg_4_a), .b(sevenseg_4_b), .e(sevenseg_4_e),
    .d(sevenseg_4_d), .c(sevenseg_4_c));  // open: dp
  not not_5 (not_5_out, l_4bitreset_c5035a69_3_b3);
  not not_6 (not_6_out, l_4bitreset_c5035a69_3_b2);
  and and_10 (and_10_out, not_5_out, not_6_out, not_7_out, not_8_out);
  not not_7 (not_7_out, l_4bitreset_c5035a69_3_b1);
  not not_8 (not_8_out, l_4bitreset_c5035a69_3_b0);
  and and_11 (and_11_out, l_4bitreset_c5035a69_3_b0, l_4bitreset_c5035a69_3_b3);
  L_4bitreset_c5035a69 l_4bitreset_c5035a69_3 (
    .Enable(in_1), .Clk(clock_1_out), .in_3(and_8_out), .B2(l_4bitreset_c5035a69_3_b2),
    .b1(l_4bitreset_c5035a69_3_b1), .B3(l_4bitreset_c5035a69_3_b3), .B0(l_4bitreset_c5035a69_3_b0));  // open: Co
  sevenseg sevenseg_5 (
    .B0(l_3_bit_adder_2dd98d25_2_out_4), .B1(l_3_bit_adder_2dd98d25_2_out_5),
    .B2(l_3_bit_adder_2dd98d25_2_out_6), .B3(1'b0), .a(sevenseg_5_a), .b(sevenseg_5_b), .c(sevenseg_5_c),
    .d(sevenseg_5_d), .e(sevenseg_5_e), .f(sevenseg_5_f), .g(sevenseg_5_g));
  _7_Segment_Display u_7_segment_display_5 (
    .g(sevenseg_5_g), .f(sevenseg_5_f), .a(sevenseg_5_a), .b(sevenseg_5_b), .e(sevenseg_5_e),
    .d(sevenseg_5_d), .c(sevenseg_5_c));  // open: dp
  sevenseg sevenseg_6 (
    .B0(l_4bitreset_c5035a69_3_b0), .B1(l_4bitreset_c5035a69_3_b1), .B2(l_4bitreset_c5035a69_3_b2),
    .B3(l_4bitreset_c5035a69_3_b3), .a(sevenseg_6_a), .b(sevenseg_6_b), .c(sevenseg_6_c), .d(sevenseg_6_d),
    .e(sevenseg_6_e), .f(sevenseg_6_f), .g(sevenseg_6_g));
  Clock clock_1 (.out(clock_1_out));
  _7_Segment_Display u_7_segment_display_6 (
    .g(sevenseg_6_g), .f(sevenseg_6_f), .a(sevenseg_6_a), .b(sevenseg_6_b), .e(sevenseg_6_e),
    .d(sevenseg_6_d), .c(sevenseg_6_c));  // open: dp
endmodule

module L_4bitreset_c5035a69 (
  input  Enable,
  input  Clk,
  input  in_3,
  output B0,
  output b1,
  output B2,
  output B3,
  output Co
);

  wire and_1_out, and_2_out, and_3_out, and_5_out, and_6_out, and_7_out, not_1_out, or_1_out;

  and and_1 (and_1_out, Enable, B0);
  and and_2 (and_2_out, and_1_out, b1);
  and and_3 (and_3_out, and_2_out, B2);
  J_K_Flip_Flop j_k_ff_1 (.J(Enable), .K(Enable), .clk(Clk), .Q(B0), .reset(or_1_out));  // open: Qn, preset
  J_K_Flip_Flop j_k_ff_2 (.J(and_1_out), .K(and_1_out), .clk(Clk), .Q(b1), .reset(or_1_out));  // open: Qn, preset
  J_K_Flip_Flop j_k_ff_3 (.J(and_2_out), .K(and_2_out), .clk(Clk), .Q(B2), .reset(or_1_out));  // open: Qn, preset
  J_K_Flip_Flop j_k_ff_4 (.J(and_3_out), .K(and_3_out), .clk(Clk), .Q(B3), .reset(or_1_out));  // open: Qn, preset
  and and_4 (Co, B3, and_3_out);
  or or_1 (or_1_out, and_7_out, in_3);
  and and_5 (and_5_out, B0, B2);
  and and_6 (and_6_out, b1, B3);
  not not_1 (not_1_out, and_5_out);
  and and_7 (and_7_out, not_1_out, and_6_out);
endmodule

module sevenseg (
  input  B0,
  input  B1,
  input  B2,
  input  B3,
  output a,
  output b,
  output c,
  output d,
  output e,
  output f,
  output g
);

  sega sega_1 (.b0(B3), .b1(B2), .b2(B1), .b3(B0), .a(a));
  segb segb_1 (.b0(B3), .b1(B2), .b2(B1), .b3(B0), .b(b));
  segc segc_1 (.b0(B3), .b1(B2), .b2(B1), .b3(B0), .c(c));
  segd segd_1 (.b0(B3), .b1(B2), .b2(B1), .b3(B0), .d(d));
  sege sege_1 (.b0(B3), .b1(B2), .b2(B1), .b3(B0), .e(e));
  segf segf_1 (.b0(B3), .b1(B2), .b2(B1), .b3(B0), .f(f));
  segg segg_1 (.b0(B3), .b1(B2), .b2(B1), .b3(B0), .g(g));
endmodule

module sega (
  input  b0,
  input  b1,
  input  b2,
  input  b3,
  output a
);

  wire and_1_out, and_2_out, and_3_out, and_4_out, and_5_out, and_6_out, not_1_out, not_2_out, not_3_out,
       not_4_out, not_5_out, not_6_out, not_7_out;

  not not_1 (not_1_out, b1);
  not not_2 (not_2_out, b3);
  not not_3 (not_3_out, b0);
  not not_4 (not_4_out, b0);
  not not_5 (not_5_out, b1);
  not not_6 (not_6_out, b2);
  not not_7 (not_7_out, b3);
  and and_1 (and_1_out, not_1_out, not_2_out);
  and and_2 (and_2_out, not_3_out, b2);
  and and_3 (and_3_out, not_4_out, b1, b3);
  and and_4 (and_4_out, b1, b2);
  and and_5 (and_5_out, b0, not_5_out, not_6_out);
  and and_6 (and_6_out, b0, not_7_out);
  or or_1 (a, and_1_out, and_2_out, and_3_out, and_4_out, and_5_out, and_6_out);
endmodule

module segb (
  input  b0,
  input  b1,
  input  b2,
  input  b3,
  output b
);

  wire and_1_out, and_2_out, and_3_out, and_4_out, and_5_out, and_6_out, not_1_out, not_2_out, not_3_out,
       not_4_out, not_5_out, not_6_out, not_7_out, not_8_out, not_9_out, not_10_out, not_11_out;

  not not_1 (not_1_out, b0);
  not not_2 (not_2_out, b1);
  not not_3 (not_3_out, b0);
  not not_4 (not_4_out, b2);
  not not_5 (not_5_out, b3);
  not not_6 (not_6_out, b1);
  not not_7 (not_7_out, b2);
  not not_8 (not_8_out, b1);
  not not_9 (not_9_out, b3);
  not not_10 (not_10_out, b0);
  not not_11 (not_11_out, b2);
  and and_1 (and_1_out, not_1_out, not_2_out);
  and and_2 (and_2_out, not_3_out, not_4_out, not_5_out);
  and and_3 (and_3_out, not_6_out, not_7_out);
  and and_4 (and_4_out, not_8_out, not_9_out);
  and and_5 (and_5_out, not_10_out, b2, b3);
  and and_6 (and_6_out, b0, not_11_out, b3);
  or or_1 (b, and_1_out, and_2_out, and_3_out, and_4_out, and_5_out, and_6_out);
endmodule

module segc (
  input  b0,
  input  b1,
  input  b2,
  input  b3,
  output c
);

  wire and_1_out, and_2_out, and_3_out, and_4_out, and_5_out, not_1_out, not_2_out, not_3_out, not_4_out,
       not_5_out, not_6_out;

  not not_1 (not_1_out, b0);
  and and_1 (and_1_out, not_1_out, not_2_out);
  not not_2 (not_2_out, b2);
  not not_3 (not_3_out, b0);
  and and_2 (and_2_out, not_3_out, b3);
  not not_4 (not_4_out, b2);
  and and_3 (and_3_out, not_4_out, b3);
  not not_5 (not_5_out, b0);
  and and_4 (and_4_out, not_5_out, b1);
  and and_5 (and_5_out, b0, not_6_out);
  not not_6 (not_6_out, b1);
  or or_1 (c, and_1_out, and_2_out, and_3_out, and_4_out, and_5_out);
endmodule

module segd (
  input  b0,
  input  b1,
  input  b2,
  input  b3,
  output d
);

  wire and_1_out, and_2_out, and_3_out, and_4_out, and_5_out, not_1_out, not_2_out, not_3_out, not_4_out,
       not_5_out, not_6_out, not_7_out;

  not not_1 (not_1_out, b0);
  not not_2 (not_2_out, b1);
  not not_3 (not_3_out, b3);
  not not_4 (not_4_out, b1);
  not not_5 (not_5_out, b2);
  not not_6 (not_6_out, b3);
  not not_7 (not_7_out, b2);
  and and_1 (and_1_out, not_1_out, not_2_out, not_3_out);
  and and_2 (and_2_out, not_4_out, b2, b3);
  and and_3 (and_3_out, b1, not_5_out, b3);
  and and_4 (and_4_out, b1, b2, not_6_out);
  and and_5 (and_5_out, b0, not_7_out);
  or or_1 (d, and_1_out, and_2_out, and_3_out, and_4_out, and_5_out);
endmodule

module sege (
  input  b0,
  input  b1,
  input  b2,
  input  b3,
  output e
);

  wire and_1_out, and_2_out, and_3_out, and_4_out, not_1_out, not_2_out, not_3_out;

  not not_1 (not_1_out, b1);
  and and_1 (and_1_out, not_1_out, not_2_out);
  not not_2 (not_2_out, b3);
  and and_2 (and_2_out, b2, not_3_out);
  not not_3 (not_3_out, b3);
  and and_3 (and_3_out, b0, b2);
  and and_4 (and_4_out, b0, b1);
  or or_1 (e, and_1_out, and_2_out, and_3_out, and_4_out);
endmodule

module segf (
  input  b0,
  input  b1,
  input  b2,
  input  b3,
  output f
);

  wire and_1_out, and_2_out, and_3_out, and_4_out, and_5_out, not_1_out, not_2_out, not_3_out, not_4_out,
       not_5_out, not_6_out;

  not not_1 (not_1_out, b2);
  and and_1 (and_1_out, not_1_out, not_2_out);
  not not_2 (not_2_out, b3);
  not not_3 (not_3_out, b0);
  and and_2 (and_2_out, not_3_out, b1, not_4_out);
  not not_4 (not_4_out, b2);
  and and_3 (and_3_out, b1, not_5_out);
  not not_5 (not_5_out, b3);
  and and_4 (and_4_out, b0, not_6_out);
  not not_6 (not_6_out, b1);
  and and_5 (and_5_out, b0, b2);
  or or_1 (f, and_1_out, and_2_out, and_3_out, and_4_out, and_5_out);
endmodule

module segg (
  input  b0,
  input  b1,
  input  b2,
  input  b3,
  output g
);

  wire and_1_out, and_2_out, and_3_out, and_4_out, and_5_out, not_1_out, not_2_out, not_3_out, not_4_out,
       not_5_out;

  not not_1 (not_1_out, b1);
  and and_1 (and_1_out, not_1_out, b2);
  and and_2 (and_2_out, b2, not_2_out);
  not not_2 (not_2_out, b3);
  not not_3 (not_3_out, b0);
  and and_3 (and_3_out, not_3_out, b1, not_4_out);
  not not_4 (not_4_out, b2);
  and and_4 (and_4_out, b0, not_5_out);
  not not_5 (not_5_out, b1);
  and and_5 (and_5_out, b0, b3);
  or or_1 (g, and_1_out, and_2_out, and_3_out, and_4_out, and_5_out);
endmodule

module countten (
  input  Enable,
  input  Clk,
  output B0,
  output b1,
  output B2,
  output B3,
  output Co
);

  wire and_1_out, and_2_out, and_3_out, and_5_out, and_6_out, and_7_out, not_1_out;

  and and_1 (and_1_out, Enable, B0);
  Clock clock_1 ();  // open: out
  and and_2 (and_2_out, and_1_out, b1);
  and and_3 (and_3_out, and_2_out, B2);
  J_K_Flip_Flop j_k_ff_1 (.J(Enable), .K(Enable), .clk(Clk), .Q(B0), .reset(and_7_out));  // open: Qn, preset
  J_K_Flip_Flop j_k_ff_2 (.J(and_1_out), .K(and_1_out), .clk(Clk), .Q(b1), .reset(and_7_out));  // open: Qn, preset
  J_K_Flip_Flop j_k_ff_3 (.J(and_2_out), .K(and_2_out), .clk(Clk), .Q(B2), .reset(and_7_out));  // open: Qn, preset
  J_K_Flip_Flop j_k_ff_4 (.J(and_3_out), .K(and_3_out), .clk(Clk), .Q(B3), .reset(and_7_out));  // open: Qn, preset
  and and_4 (Co, B3, and_3_out);
  not not_1 (not_1_out, B2);
  and and_5 (and_5_out, B0, not_1_out);
  and and_6 (and_6_out, b1, B3);
  and and_7 (and_7_out, and_5_out, and_6_out);
endmodule

module threebitmodfive (
  input  in_1,
  input  in_2,
  input  in_3,
  output out_4,
  output out_5,
  output out_6
);

  wire and_1_out, j_k_ff_1_qn, j_k_ff_2_qn, not_1_out, or_1_out;

  J_K_Flip_Flop j_k_ff_1 (
    .J(in_2), .K(in_2), .clk(in_3), .Q(out_4), .Qn(j_k_ff_1_qn), .reset(or_1_out));  // open: preset
  J_K_Flip_Flop j_k_ff_2 (
    .J(in_2), .K(in_2), .clk(j_k_ff_1_qn), .Q(out_5), .Qn(j_k_ff_2_qn), .reset(or_1_out));  // open: preset
  not not_1 (not_1_out, out_4);
  J_K_Flip_Flop j_k_ff_3 (.J(in_2), .K(in_2), .clk(j_k_ff_2_qn), .Q(out_6), .reset(or_1_out));  // open: Qn, preset
  and and_1 (and_1_out, out_6, out_5, not_1_out);
  or or_1 (or_1_out, and_1_out, in_1);
endmodule

module twobitmodthree (
  input  in_1,
  input  in_2,
  input  in_3,
  output out_4,
  output out_5
);

  wire and_1_out, j_k_ff_1_qn, or_1_out;

  J_K_Flip_Flop j_k_ff_1 (
    .J(in_2), .K(in_2), .clk(in_3), .Q(out_4), .Qn(j_k_ff_1_qn), .reset(or_1_out));  // open: preset
  J_K_Flip_Flop j_k_ff_2 (.J(in_2), .K(in_2), .clk(j_k_ff_1_qn), .Q(out_5), .reset(or_1_out));  // open: Qn, preset
  and and_1 (and_1_out, out_4, out_5);
  or or_1 (or_1_out, and_1_out, in_1);
endmodule
